# Fritzing sketch Schema_circuit (saved by Fritzing 1.0.6)
circuit board: 8.46667cm x 5.64444cm
breadboards: 1

parts:
  Part1 = Arduino Uno (Rev3) - ICSP
  Part2 = RFID-RC522-v2
  Part3 = LCD1602-I2C
  SERVO1 = Tower Pro SG90 servo [part_number=101246]
  C1 = Electrolytic Capacitor [capacitance=0.22mF voltage=10V package="200 mil [THT, electrolytic]"]
  LED1 = LED - 3mm [color="Red (633nm)" current=0.030A package="3 mm [THT]"]
  R1 = Resistor [tolerance=±5% resistance=220 power=0.25W package="1206 [SMD]"]
  LED2 = LED - 3mm [color="Green (570nm)" current=0.030A package="3 mm [THT]"]
  R2 = Resistor [tolerance=±5% resistance=220 power=0.25W package="1206 [SMD]"]

nets:
  N1: Part1.A4/SDA, Part3.SDA
  N2: Part1.A5/SCL, Part3.SCL
  N3: Part1.D9_PWM, Part2.RST
  N4: Part1.D10_PWM/SS, Part2.SDA
  N5: Part1.D11_PWM/MOSI, Part2.MOSI
  N6: Part1.D12/MISO, Part2.MISO
  N7: Part1.D13/SCK, Part2.SCK
  N8: Part1.D3_PWM, SERVO1.Signal
  N9: Part1.D5_PWM, R2.Pin_1
  N10: Part1.D6_PWM, R1.Pin_0
  3V3: Part1.3V3, Part2.3.3V
  5V: Part1.5V, Part3.VCC, SERVO1.+5V, C1.+
  GND: Part1.GND, Part2.GND, Part3.GND, SERVO1.GND, C1.-, LED1.cathode, LED2.cathode
  N11: LED1.anode, R1.Pin_1
  N12: LED2.anode, R2.Pin_0

custom parts:
  RFID-RC522-v2: A simple China made RFID-RC522 Reader; do check the pin labels, as this is a MFRC522 based clone.
  LCD1602-I2C: A standard character display, usually with 2x16 characters. Comes in many colors with LCM1602 IIC attached.
  Tower Pro SG90 servo: Original file by John De Cristofaro http://www.adafruit.com/products/1449 Adafruit Feedback Servo (Small) Edited by: e-radionica.com 28/9/2015
